// Logisim project part2.circ as structural Verilog: 1 circuit, main circuit main
module main (
  input  MuxCSel,
  input  [3:0] FunSel,
  input  [1:0] OutASel,
  input  [1:0] OutBSel,
  input  [1:0] FunSel_2,
  input  [3:0] RegSel,
  input  [1:0] MuxASel,
  input  [1:0] MuxBSel,
  input  in_9,
  input  in_10,
  input  in_11,
  input  in_12,
  input  [1:0] OutCSel,
  input  [1:0] OutDSel,
  input  [1:0] FunSel_3,
  input  [3:0] RegSel_2,
  input  L_H,
  input  Enable,
  input  [1:0] FunSel_4,
  output [7:0] out_20,
  output [3:0] out_21,
  output [7:0] out_22
);

  wire clock_1_out, n4_register_bank_1_p7;
  wire [3:0] main_2_p6;
  wire [7:0] main_1_p1, multiplexer_1_out, multiplexer_2_out, multiplexer_3_out, n3_register_bank_1_p7,
       n3_register_bank_1_p8, n4_register_bank_1_p8;
  wire [15:8] main_1_p6;

  Clock clock_1 (.out(clock_1_out));
  Multiplexer #(.select(2), .width(8), .enable("false")) multiplexer_1 (
    .in0(out_22), .in1(main_1_p1), .in2(n3_register_bank_1_p7), .in3(out_20), .out(multiplexer_1_out),
    .sel(MuxASel));
  // _4_register_bank 4_register_bank_1: pin names not known; wires that end beside it: RegSel, multiplexer_1_out, FunSel_2, OutASel, clock_1_out, OutBSel, n4_register_bank_1_p7, n4_register_bank_1_p8
  Multiplexer #(.select(2), .width(8), .enable("false")) multiplexer_2 (
    .in0(out_22), .in1(out_22), .in2(main_1_p1), .in3(out_20), .out(multiplexer_2_out), .sel(MuxBSel));
  // _2c_main main_1: pin names not known; wires that end beside it: main_1_p1, L_H, FunSel_4, clock_1_out, Enable, {main_1_p6, out_22}
  Multiplexer #(.width(8), .enable("false")) multiplexer_3 (
    .in0(multiplexer_1_out), .in1(n4_register_bank_1_p8), .out(multiplexer_3_out), .sel(MuxCSel));
  // alu2_main main_2: pin names not known; wires that end beside it: multiplexer_3_out, n4_register_bank_1_p7, FunSel, out_21[2], out_20, main_2_p6
  // _3_register_bank 3_register_bank_1: pin names not known; wires that end beside it: RegSel_2, multiplexer_2_out, FunSel_3, OutCSel, clock_1_out, OutDSel, n3_register_bank_1_p7, n3_register_bank_1_p8
  Register #(.width(4)) register_1 (.D(main_2_p6), .en(1'b1), .Q(out_21), .clk(clock_1_out));  // open: clr
  RAM #(.bus("separate")) ram_1 (
    .addr(n3_register_bank_1_p8), .din(out_20), .data(main_1_p1), .str(in_9), .sel(in_10), .clk(clock_1_out),
    .ld(in_11), .clr(in_12));

  // Notes on the sheet:
  //   A
  //   B
  //   C
endmodule
